// Logisim project RPS.circ as structural Verilog: 1 circuit, main circuit main
module main (
  input  Rock,
  input  Paper,
  input  Scissors,
  input  Rock_2,
  input  Paper_2,
  input  Scissors_2,
  output Player_A_Wins,
  output Player_B_Wins,
  output INVALID_INPUT__SELECT_ONE_OPTION,
  output INVALID_INPUT__SELECT_ONE_OPTION_2,
  output INVALID_INPUT__SELECT_ONE_OPTION_3
);

  and and_1 (Player_B_Wins, Rock, Paper_2);
  and and_2 (Player_A_Wins, Scissors, Paper_2);
  and and_3 (INVALID_INPUT__SELECT_ONE_OPTION, Rock, Paper);
  and and_4 (INVALID_INPUT__SELECT_ONE_OPTION_2, Scissors, Rock);
  and and_5 (INVALID_INPUT__SELECT_ONE_OPTION_3, Paper, Scissors);

  // Notes on the sheet:
  //   Player A
  //   Player B
endmodule
